// Logisim project Elevator Control Project.circ as structural Verilog: 11 circuits, main circuit main
module main (
  output [2:0] out_1,
  output [2:0] Final_Status
);

  wire clock_1_out, i_ps_to_7_seg_1_a, i_ps_to_7_seg_1_b, i_ps_to_7_seg_1_c, i_ps_to_7_seg_1_d,
       i_ps_to_7_seg_1_e, i_ps_to_7_seg_1_f, i_ps_to_7_seg_1_g;
  wire [1:0] finding_yd_1_yd;
  wire [2:0] Ground_out, latching_section_1_i2__i1__i0_2, pri_encoder_up_1_q2__q1__q0;
  wire [3:0] _0U_out, i_ps_for_arrow_1_out_2, i_ps_for_arrow_1_out_3, i_ps_for_arrow_1_out_4,
       latching_section_1_o2d__o1u__o1d__o0u_2;
  wire [4:0] Decoder_y7__y6__y5__y4__y3;

  Button _2D (.out(_0U_out[3]));
  Button _1U (.out(_0U_out[2]));
  Button _1D (.out(_0U_out[1]));
  Button _0U (.out(_0U_out[0]));
  Button Second (.out(Ground_out[2]));
  Button First (.out(Ground_out[1]));
  Button Ground (.out(Ground_out[0]));
  Latching_Section latching_section_1 (
    .O2d__O1u__O1d__O0u(_0U_out), .I2__I1__I0(Ground_out), .Yu__Yd(finding_yd_1_yd),
    .S2__S1__S0(Final_Status), .O2d__O1u__O1d__O0u_2(latching_section_1_o2d__o1u__o1d__o0u_2),
    .I2__I1__I0_2(latching_section_1_i2__i1__i0_2));
  Finding_Yu finding_yu_1 (
    .O2d__O1u__O1d__O0u(latching_section_1_o2d__o1u__o1d__o0u_2),
    .I2__I1__I0(latching_section_1_i2__i1__i0_2), .S2__S1__S0(Final_Status),
    .Current_Yu__Yd(finding_yd_1_yd), .Yu(finding_yd_1_yd[1]));
  Finding_Yd finding_yd_1 (
    .O2d__O1u__O1d__O0u(latching_section_1_o2d__o1u__o1d__o0u_2),
    .I2__I1__I0(latching_section_1_i2__i1__i0_2), .S2__S1__S0(Final_Status),
    .Current_Yu__Yd(finding_yd_1_yd), .Yd(finding_yd_1_yd[0]));
  Pri_Encoder_Up pri_encoder_up_1 (
    .O2d__O1u__O1d__O0u(latching_section_1_o2d__o1u__o1d__o0u_2),
    .I2__I1__I0(latching_section_1_i2__i1__i0_2), .Yu__Yd(finding_yd_1_yd),
    .Q2__Q1__Q0(pri_encoder_up_1_q2__q1__q0));
  Pri_Encoder_Down pri_encoder_down_1 (
    .O2d__O1u__O1d__O0u(latching_section_1_o2d__o1u__o1d__o0u_2),
    .I2__I1__I0(latching_section_1_i2__i1__i0_2), .Yu__Yd(finding_yd_1_yd),
    .Q2__Q1__Q0(pri_encoder_up_1_q2__q1__q0));
  Calculating_Status Calculating_Status (
    .Y7__Y6__Y5__Y4__Y3(Decoder_y7__y6__y5__y4__y3), .Yu__Yd(finding_yd_1_yd), .Old_Status(Final_Status),
    .S2__S1__S0(out_1));
  Decoder Decoder (.Q2__Q1__Q0(pri_encoder_up_1_q2__q1__q0), .Y7__Y6__Y5__Y4__Y3(Decoder_y7__y6__y5__y4__y3));
  Register #(.width(3)) Delay (.D(out_1), .Q(Final_Status), .clk(clock_1_out));  // open: en, clr
  Clock clock_1 (.out(clock_1_out));
  I_Ps_to_7_Seg i_ps_to_7_seg_1 (
    .S2__S1__S0(Final_Status), .a(i_ps_to_7_seg_1_a), .b(i_ps_to_7_seg_1_b), .c(i_ps_to_7_seg_1_c),
    .d(i_ps_to_7_seg_1_d), .e(i_ps_to_7_seg_1_e), .f(i_ps_to_7_seg_1_f), .g(i_ps_to_7_seg_1_g));
  I_Ps_for_Arrow i_ps_for_arrow_1 (
    .Yu__Yd(finding_yd_1_yd), .out_2(i_ps_for_arrow_1_out_2), .out_3(i_ps_for_arrow_1_out_3),
    .out_4(i_ps_for_arrow_1_out_4));
  _7_Segment_Display u_7_segment_display_1 (
    .g(i_ps_to_7_seg_1_g), .f(i_ps_to_7_seg_1_f), .a(i_ps_to_7_seg_1_a), .b(i_ps_to_7_seg_1_b),
    .e(i_ps_to_7_seg_1_e), .d(i_ps_to_7_seg_1_d), .c(i_ps_to_7_seg_1_c));  // open: dp
  DotMatrix #(.matrixcols(3), .matrixrows(4), .dotshape("circle")) dotmatrix_1 (
    .col0(i_ps_for_arrow_1_out_2), .col1(i_ps_for_arrow_1_out_3), .col2(i_ps_for_arrow_1_out_4));

  // Notes on the sheet:
  //   From outside
  //   From inside
  //   Latching Section
  //   Directional Control Unit
  //   Up Controller
  //   Down Controller
  //   Output Display
  //   Direction
endmodule

module Latching_Section (
  input  [3:0] O2d__O1u__O1d__O0u,
  input  [2:0] I2__I1__I0,
  input  [1:0] Yu__Yd,
  input  [2:0] S2__S1__S0,
  output [3:0] O2d__O1u__O1d__O0u_2,
  output [2:0] I2__I1__I0_2
);

  wire and_1_out, and_2_out;

  and and_1 (and_1_out, ~Yu__Yd[0], S2__S1__S0[1]);  // AND_Gate
  and and_2 (and_2_out, ~Yu__Yd[1], S2__S1__S0[1]);  // AND_Gate
  J_K_Flip_Flop j_k_ff_1 (
    .J(1'b1), .clk(O2d__O1u__O1d__O0u[3]), .K(1'b1), .Q(O2d__O1u__O1d__O0u_2[3]), .reset(S2__S1__S0[2]));  // open: Qn, preset, en
  J_K_Flip_Flop j_k_ff_2 (
    .J(1'b1), .clk(O2d__O1u__O1d__O0u[2]), .K(1'b1), .Q(O2d__O1u__O1d__O0u_2[2]), .reset(and_1_out));  // open: Qn, preset, en
  J_K_Flip_Flop j_k_ff_3 (
    .J(1'b1), .clk(O2d__O1u__O1d__O0u[1]), .K(1'b1), .Q(O2d__O1u__O1d__O0u_2[1]), .reset(and_2_out));  // open: Qn, preset, en
  J_K_Flip_Flop j_k_ff_4 (
    .J(1'b1), .clk(O2d__O1u__O1d__O0u[0]), .K(1'b1), .Q(O2d__O1u__O1d__O0u_2[0]), .reset(S2__S1__S0[0]));  // open: Qn, preset, en
  J_K_Flip_Flop j_k_ff_5 (
    .J(1'b1), .clk(I2__I1__I0[2]), .K(1'b1), .Q(I2__I1__I0_2[2]), .reset(S2__S1__S0[2]));  // open: Qn, preset, en
  J_K_Flip_Flop j_k_ff_6 (
    .J(1'b1), .clk(I2__I1__I0[1]), .K(1'b1), .Q(I2__I1__I0_2[1]), .reset(S2__S1__S0[1]));  // open: Qn, preset, en
  J_K_Flip_Flop j_k_ff_7 (
    .J(1'b1), .clk(I2__I1__I0[0]), .K(1'b1), .Q(I2__I1__I0_2[0]), .reset(S2__S1__S0[0]));  // open: Qn, preset, en
endmodule

module Mux_for_Status (
  input  [2:0] S2__S1__S0,
  input  [1:0] Yu__Yd,
  input  [2:0] Old_Status,
  output [2:0] Output_Status
);

  wire [1:0] and_2_out;
  wire [2:0] undriven;

  and and_1 (and_2_out[1], ~Yu__Yd[0], ~Yu__Yd[1]);  // AND_Gate
  and and_2 (and_2_out[0], ~Old_Status[0], ~Old_Status[1], ~Old_Status[2]);  // AND_Gate
  Multiplexer #(.select(2), .width(3)) multiplexer_1 (
    .in0(S2__S1__S0), .in1(undriven), .in2(Old_Status), .in3(3'b001), .out(Output_Status), .sel(and_2_out));  // open: en

  // Notes on the sheet:
  //   Calculated Status
  //   001
endmodule

module Calculating_Status (
  input  [1:0] Yu__Yd,
  input  [4:0] Y7__Y6__Y5__Y4__Y3,
  input  [2:0] Old_Status,
  output [2:0] S2__S1__S0
);

  wire or_1_out, or_2_out, or_3_out, Yd_Yu_prime_out, Yu_Yd_prime_out;
  wire [2:0] and_1_out;

  and Yd_Yu_prime (Yd_Yu_prime_out, Yu__Yd[0], ~Yu__Yd[1]);  // AND_Gate
  and Yu_Yd_prime (Yu_Yd_prime_out, Yu__Yd[1], ~Yu__Yd[0]);  // AND_Gate
  or or_1 (or_1_out, Yu_Yd_prime_out, Yd_Yu_prime_out);
  or or_2 (or_2_out, Y7__Y6__Y5__Y4__Y3[1], Y7__Y6__Y5__Y4__Y3[2]);
  or or_3 (or_3_out, Y7__Y6__Y5__Y4__Y3[3], Y7__Y6__Y5__Y4__Y3[0], Y7__Y6__Y5__Y4__Y3[4]);
  and and_1 (and_1_out[0], Yd_Yu_prime_out, or_2_out);
  and and_2 (and_1_out[1], or_1_out, or_3_out);
  and and_3 (and_1_out[2], Yu_Yd_prime_out, or_2_out);
  Mux_for_Status mux_for_status_1 (
    .S2__S1__S0(and_1_out), .Yu__Yd(Yu__Yd), .Old_Status(Old_Status), .Output_Status(S2__S1__S0));

  // Notes on the sheet:
  //   Direction Variables
  //   Decoder O/Ps
  //   Xnor(Yu, Yd)
  //   Y4 + Y5
  //   Y3 + Y6 + Y7
endmodule

module Pri_Encoder_Up (
  input  [3:0] O2d__O1u__O1d__O0u,
  input  [2:0] I2__I1__I0,
  input  [1:0] Yu__Yd,
  output [2:0] Q2__Q1__Q0
);

  wire and_1_out;

  Priority_Encoder priority_encoder_1 (
    .in0(1'b1), .in1(1'b1), .in2(1'b1), .in3(O2d__O1u__O1d__O0u[1]), .in4(O2d__O1u__O1d__O0u[3]),
    .in5(I2__I1__I0[2]), .in6(O2d__O1u__O1d__O0u[2]), .in7(I2__I1__I0[1]), .out(Q2__Q1__Q0), .en_in(and_1_out));  // open: gs, en_out
  and and_1 (and_1_out, Yu__Yd[1], ~Yu__Yd[0]);  // AND_Gate

  // Notes on the sheet:
  //   O1d, O2d, I2, O1u, I1
endmodule

module Pri_Encoder_Down (
  input  [3:0] O2d__O1u__O1d__O0u,
  input  [2:0] I2__I1__I0,
  input  [1:0] Yu__Yd,
  output [2:0] Q2__Q1__Q0
);

  wire and_1_out;

  Priority_Encoder priority_encoder_1 (
    .in0(1'b1), .in1(1'b1), .in2(1'b1), .in3(O2d__O1u__O1d__O0u[2]), .in4(O2d__O1u__O1d__O0u[0]),
    .in5(I2__I1__I0[0]), .in6(O2d__O1u__O1d__O0u[1]), .in7(I2__I1__I0[1]), .out(Q2__Q1__Q0), .en_in(and_1_out));  // open: gs, en_out
  and and_1 (and_1_out, ~Yu__Yd[1], Yu__Yd[0]);  // AND_Gate

  // Notes on the sheet:
  //   O1u, O0u, I0, O1d, I1
endmodule

module Decoder (
  input  [2:0] Q2__Q1__Q0,
  output [4:0] Y7__Y6__Y5__Y4__Y3
);

  Decoder_part #(.select(3)) decoder_1 (
    .out3(Y7__Y6__Y5__Y4__Y3[0]), .out4(Y7__Y6__Y5__Y4__Y3[1]), .out5(Y7__Y6__Y5__Y4__Y3[2]),
    .out6(Y7__Y6__Y5__Y4__Y3[3]), .out7(Y7__Y6__Y5__Y4__Y3[4]), .sel(Q2__Q1__Q0), .en(1'b1));  // open: out0, out1, out2
endmodule

module Finding_Yu (
  input  [1:0] Current_Yu__Yd,
  input  [3:0] O2d__O1u__O1d__O0u,
  input  [2:0] I2__I1__I0,
  input  [2:0] S2__S1__S0,
  output Yu
);

  wire and_1_out, and_2_out, or_1_out, or_2_out, or_3_out;

  or or_1 (or_1_out, I2__I1__I0[2], O2d__O1u__O1d__O0u[2], O2d__O1u__O1d__O0u[3]);
  or or_2 (or_2_out, or_1_out, I2__I1__I0[1], O2d__O1u__O1d__O0u[1]);
  and and_1 (and_1_out, or_2_out, S2__S1__S0[0]);
  or or_3 (or_3_out, and_1_out, and_2_out);
  and and_2 (and_2_out, or_1_out, S2__S1__S0[1]);
  and and_3 (Yu, ~Current_Yu__Yd[0], or_3_out);  // AND_Gate

  // Notes on the sheet:
  //   Yu = Yd' (S0 (O1d + O1u + O2d + I1 + I2) + S1 (O2d + O1u + I2))
endmodule

module Finding_Yd (
  input  [1:0] Current_Yu__Yd,
  input  [3:0] O2d__O1u__O1d__O0u,
  input  [2:0] I2__I1__I0,
  input  [2:0] S2__S1__S0,
  output Yd
);

  wire and_1_out, and_2_out, or_1_out, or_2_out, or_3_out;

  or or_1 (or_1_out, O2d__O1u__O1d__O0u[0], O2d__O1u__O1d__O0u[1], I2__I1__I0[0]);
  or or_2 (or_2_out, or_1_out, O2d__O1u__O1d__O0u[2], I2__I1__I0[1]);
  and and_1 (and_1_out, or_2_out, S2__S1__S0[2]);
  or or_3 (or_3_out, and_1_out, and_2_out);
  and and_2 (and_2_out, or_1_out, S2__S1__S0[1]);
  and and_3 (Yd, ~Current_Yu__Yd[1], or_3_out);  // AND_Gate

  // Notes on the sheet:
  //   Yd = Yu' (S2 (O1u + O1d + O0u + I1 + I0) + S1 (O1d + O0u + I0))
endmodule

module I_Ps_to_7_Seg (
  input  [2:0] S2__S1__S0,
  output a,
  output b,
  output c,
  output d,
  output e,
  output f,
  output g
);

  not not_1 (a, S2__S1__S0[1]);
  not not_2 (b, S2__S1__S0[0]);
  not not_3 (c, S2__S1__S0[2]);
  not not_4 (d, S2__S1__S0[1]);
  not not_5 (e, S2__S1__S0[1]);

  assign f = S2__S1__S0[0];
  assign g = S2__S1__S0[2];
endmodule

module I_Ps_for_Arrow (
  input  [1:0] Yu__Yd,
  output [3:0] out_2,
  output [3:0] out_3,
  output [3:0] out_4
);

  or or_1 (out_3[0], Yu__Yd[1], Yu__Yd[0]);
  not not_1 (out_2[1], Yu__Yd[1]);
  not not_2 (out_4[1], Yu__Yd[1]);
  not not_3 (out_2[2], Yu__Yd[0]);
  not not_4 (out_4[2], Yu__Yd[0]);
  or or_2 (out_3[3], Yu__Yd[1], Yu__Yd[0]);

  assign {out_2[3], out_2[0]} = 2'b00;
  assign out_3[2:1] = 2'b11;
  assign {out_4[3], out_4[0]} = 2'b00;
endmodule
